// Logisim project ALU.circ as structural Verilog: 6 circuits, main circuit Add/Sub
module Add_Sub (
  input  in_1,
  input  [1:0] A,
  input  [1:0] B,
  output [1:0] OUTPUT,
  output CARRY
);

  wire adder_1_cout, xor_1_out, xor_2_out;

  xor xor_1 (xor_1_out, in_1, B[0]);
  xor xor_2 (xor_2_out, in_1, B[1]);
  Adder #(.width(1)) adder_1 (.a(A[0]), .b(xor_1_out), .out(OUTPUT[0]), .cin(in_1), .cout(adder_1_cout));
  Adder #(.width(1)) adder_2 (.a(A[1]), .b(xor_2_out), .out(OUTPUT[1]), .cin(adder_1_cout), .cout(CARRY));

  // Notes on the sheet:
  //   A0
  //   B0
  //   A1
  //   B1
  //   Add/Sub Control
endmodule

module bitwise_OR (
  input  [1:0] A,
  input  [1:0] B,
  output [1:0] out_3
);

  or or_1 (out_3[0], A[0], B[0]);
  or or_2 (out_3[1], A[1], B[1]);
endmodule

module bitwise_AND (
  input  [1:0] A,
  input  [1:0] B,
  output [1:0] out_3
);

  and and_1 (out_3[0], A[0], B[0]);
  and and_2 (out_3[1], A[1], B[1]);
endmodule

module Increment_Decre (
  input  in_1,
  input  [1:0] A,
  input  in_3,
  input  in_4,
  output [1:0] out_5,
  output out_6
);

  wire adder_1_cout, xor_1_out, xor_2_out;

  xor xor_1 (xor_1_out, in_1, in_3);
  xor xor_2 (xor_2_out, in_1, in_4);
  Adder #(.width(1)) adder_1 (.a(A[0]), .b(xor_1_out), .out(out_5[0]), .cin(in_1), .cout(adder_1_cout));
  Adder #(.width(1)) adder_2 (.a(A[1]), .b(xor_2_out), .out(out_5[1]), .cin(adder_1_cout), .cout(out_6));
endmodule

module leftShifter (
  input  [1:0] A,
  input  shift,
  input  in_3,
  output [1:0] \output 
);

  Multiplexer #(.enable("false")) multiplexer_1 (.in0(A[1]), .in1(A[0]), .out(\output [0]), .sel(shift));
  Multiplexer #(.disabled(0), .enable("false")) multiplexer_2 (.in0(A[0]), .in1(in_3), .out(\output [1]), .sel(shift));
endmodule

module rightShifter (
  input  in_1,
  input  [1:0] A,
  input  enable,
  output [1:0] bit1
);

  Multiplexer #(.enable("false")) multiplexer_1 (.in0(A[0]), .in1(in_1), .out(bit1[0]), .sel(enable));
  Multiplexer #(.disabled(0), .enable("false")) multiplexer_2 (.in0(A[1]), .in1(A[0]), .out(bit1[1]), .sel(enable));
endmodule
